// Logisim project e2.circ as structural Verilog: 1 circuit, main circuit main
module main (
  input  a,
  input  b,
  input  in_3,
  input  c,
  input  d
);

  wire and_1_out, nand_1_out, not_1_out, not_2_out, or_1_out;

  not not_1 (not_1_out, a);
  not not_2 (not_2_out, c);
  and and_1 (and_1_out, not_1_out, b);
  nand nand_1 (nand_1_out, not_2_out, d);
  or or_1 (or_1_out, and_1_out, nand_1_out);

  // Notes on the sheet:
  //   !a*b + !(!c*d)
endmodule
