// Logisim project e1.circ as structural Verilog: 1 circuit, main circuit main
module main (
  input  a,
  input  b,
  input  in_3,
  input  c,
  input  d
);

  wire nand_1_out, nand_2_out, nand_3_out, not_1_out, not_2_out, not_3_out, not_4_out;

  nand nand_1 (nand_1_out, a, b);
  not not_1 (not_1_out, c);
  not not_2 (not_2_out, d);
  not not_3 (not_3_out, nand_1_out);
  nand nand_2 (nand_2_out, not_1_out, not_2_out);
  nand nand_3 (nand_3_out, not_3_out, nand_2_out);
  not not_4 (not_4_out, nand_3_out);

  // Notes on the sheet:
  //   (a*b) * !(!c * !d)
endmodule
