// Logisim project e1.circ as structural Verilog: 1 circuit, main circuit main
module main (
  input  A,
  input  B,
  input  OUTPUT,
  input  C,
  input  D
);

  wire and_1_out, nor_1_out, not_1_out, not_2_out, or_1_out;

  not not_1 (not_1_out, A);
  not not_2 (not_2_out, B);
  or or_1 (or_1_out, C, D);
  nor nor_1 (nor_1_out, not_1_out, not_2_out);
  and and_1 (and_1_out, nor_1_out, or_1_out);

  // Notes on the sheet:
  //   !(!a+!b) * (C +D)
endmodule
