// Logisim project e2.circ as structural Verilog: 1 circuit, main circuit main
module main (
  input  a,
  input  b,
  input  c,
  input  in_4,
  input  d
);

  wire nand_1_out, nand_2_out, nand_3_out, not_1_out, not_2_out, not_3_out;

  not not_1 (not_1_out, a);
  not not_2 (not_2_out, c);
  nand nand_1 (nand_1_out, not_1_out, b);
  not not_3 (not_3_out, nand_2_out);
  nand nand_2 (nand_2_out, not_2_out, d);
  nand nand_3 (nand_3_out, nand_1_out, not_3_out);

  // Notes on the sheet:
  //   !(!(!a*b)*(!c*d))
endmodule
