// Logisim project e2.circ as structural Verilog: 1 circuit, main circuit main
module main (
  input  a,
  input  b,
  input  c,
  input  d
);

  wire nor_1_out, nor_2_out, nor_3_out, not_1_out, not_2_out, not_3_out;

  not not_1 (not_1_out, b);
  not not_2 (not_2_out, d);
  nor nor_1 (nor_1_out, a, not_1_out);
  not not_3 (not_3_out, nor_2_out);
  nor nor_2 (nor_2_out, c, not_2_out);
  nor nor_3 (nor_3_out, nor_1_out, not_3_out);
  // NOT_Gate not_4 has open pins: in=nor_3_out, out=open

  // Notes on the sheet:
  //   !(a+!b) + (c+!d)
endmodule
