// Logisim project multiplicador.circ as structural Verilog: 1 circuit, main circuit main
// multiplicador
module main (
  input  [3:0] A,
  input  [3:0] B,
  input  [3:0] OUTPUT
);

  wire A1_B0_out, AO_B1_out;
  wire [0:0] AO_B0_out;

  and AO_B0 (AO_B0_out[0], B[0], A[0]);
  and A1_B0 (A1_B0_out, A[1], B[0]);
  // AND_Gate A2_B0 has open pins: in1=B[0], out=open
  // AND_Gate A3_B0 has open pins: in0=A[3], in1=B[0], out=open
  // HALF_ADDER half_adder_1: pin names not known
  and AO_B1 (AO_B1_out, A[0], B[1]);
  // AND_Gate A1_B1 has open pins: in0=A[1], in1=B[1], out=open
  // AND_Gate A2_B1 has open pins: in0=A[2], in1=B[1], out=open
  // AND_Gate A3_B1 has open pins: in0=A[3], in1=B[1], out=open
  // AND_Gate AO_B2 has open pins: in0=A[0], in1=B[2], out=open
  // AND_Gate A1_B2 has open pins: in0=A[1], in1=B[2], out=open
  // AND_Gate A2_B2 has open pins: in0=A[2], in1=B[2], out=open
  // AND_Gate A3_B2 has open pins: in0=A[3], in1=B[2], out=open
  // AND_Gate AO_B3 has open pins: in0=A[0], in1=B[3], out=open
  // AND_Gate A1_B3 has open pins: in0=A[1], in1=B[3], out=open
  // AND_Gate A2_B3 has open pins: in0=A[2], in1=B[3], out=open
  // AND_Gate A3_B3 has open pins: in0=A[3], in1=B[3], out=open
endmodule
