// Logisim project mux 2-1.circ as structural Verilog: 1 circuit, main circuit main
// MUX 2-1
module main (
  input  A,
  input  B,
  input  S,
  output OUT
);

  wire and_1_out, and_2_out, not_1_out;

  and and_1 (and_1_out, A, not_1_out);
  and and_2 (and_2_out, B, S);
  not not_1 (not_1_out, S);
  or or_1 (OUT, and_1_out, and_2_out);

  // Notes on the sheet:
  //   b*s + a *!s
endmodule
