// Logisim project mux 4-1 (4 bits).circ as structural Verilog: 1 circuit, main circuit main
// MUX 4-1 (4 bits)
module main (
  input  [3:0] A,
  input  [3:0] B,
  input  [3:0] C,
  input  [3:0] D,
  input  [1:0] S,
  output [3:0] OUT
);

  mux_4_1_main main_1 (.A(A[0]), .B(B[0]), .C(C[0]), .D(D[0]), .S(S), .out(OUT[0]));
  mux_4_1_main main_2 (.A(A[1]), .B(B[1]), .C(C[1]), .D(D[1]), .S(S), .out(OUT[1]));
  mux_4_1_main main_3 (.A(A[2]), .B(B[2]), .C(C[2]), .D(D[2]), .S(S), .out(OUT[2]));
  mux_4_1_main main_4 (.A(A[3]), .B(A[3]), .C(C[3]), .D(D[3]), .S(S), .out(OUT[3]));

  assign B[3] = A[3];
endmodule
