// Logisim project mux 4-1.circ as structural Verilog: 1 circuit, main circuit main
// MUX 4-1
module main (
  input  A,
  input  B,
  input  C,
  input  D,
  input  [1:0] S,
  output out
);

  wire main_1_out, main_2_out;

  mux_2_1_main main_1 (.A(A), .B(B), .S(S[0]), .OUT(main_1_out));
  mux_2_1_main main_2 (.A(C), .B(D), .S(S[0]), .OUT(main_2_out));
  mux_2_1_main main_3 (.A(main_1_out), .B(main_2_out), .S(S[1]), .OUT(out));
endmodule
