// Logisim project mux41.circ as structural Verilog: 1 circuit, main circuit MUX(4:1)
module MUX_4_1 (
  input  D0,
  input  D1,
  input  D2,
  input  D3,
  input  S1,
  input  S0,
  output OUTPUT
);

  wire and_1_out, and_2_out, and_3_out, and_4_out, not_1_out, not_2_out;

  not not_1 (not_1_out, S1);
  not not_2 (not_2_out, S0);
  and and_1 (and_1_out, D0, not_2_out, not_1_out);
  and and_2 (and_2_out, D1, S0, not_1_out);
  and and_3 (and_3_out, D2, not_2_out, S1);
  and and_4 (and_4_out, D3, S1, S0);
  or or_1 (OUTPUT, and_1_out, and_2_out, and_3_out, and_4_out);

  // Notes on the sheet:
  //   O = S1*S0*D3 + S1 *!S0 *D2 + !S1*S0*D2 + !S1 + !S0 *D0
endmodule
