// Logisim project subtrator.circ as structural Verilog: 1 circuit, main circuit SUBTRATOR
module SUBTRATOR (
  input  [3:0] A,
  input  [3:0] B,
  output [3:0] OUT
);

  wire [3:0] not_1_out, somador_1_output;

  assign not_1_out = ~B;  // NOT_Gate not_1, 4 bits wide
  SOMADOR somador_1 (.INPUT_1(not_1_out), .INPUT_2(4'b0001), .OUTPUT(somador_1_output));  // open: CARRY_OUT
  SOMADOR somador_2 (.INPUT_1(A), .INPUT_2(somador_1_output), .OUTPUT(OUT));  // open: CARRY_OUT

  // Notes on the sheet:
  //   GAMBIARRA
  //   Em vez de fazer todo o circuito, realizei o complemento de dois e a soma.
endmodule
