// Logisim project ula.circ as structural Verilog: 1 circuit, main circuit main
// ULA
module main (
  input  [9:0] \Código ,
  output [3:0] OUT
);

  wire [0:0] comparador_1_output;
  wire [3:0] multiplicador_1_out, somador_1_output, subtrator_1_out;

  SUBTRATOR subtrator_1 (.A(\Código [7:4]), .B(\Código [3:0]), .OUT(subtrator_1_out));
  MULTIPLICADOR multiplicador_1 (.A(\Código [7:4]), .B(\Código [3:0]), .out(multiplicador_1_out));  // open: CARRY_OUT
  COMPARADOR comparador_1 (.INPUT_2(\Código [7:4]), .INPUT_1(\Código [3:0]), .OUTPUT(comparador_1_output[0]));
  SOMADOR somador_1 (.INPUT_1(\Código [7:4]), .INPUT_2(\Código [3:0]), .OUTPUT(somador_1_output));  // open: CARRY_OUT
  mux_4_1__4_bits__main main_1 (
    .A(somador_1_output), .B(subtrator_1_out), .C(multiplicador_1_out), .D({3'b000, comparador_1_output[0]}),
    .S(\Código [9:8]), .OUT(OUT));

  // Notes on the sheet:
  //   Opcodes - Operação:
  //   00 - ADD - 00
  //   01  - SUB - 01
  //   02 - MULT - 10
  //   03 - COMP - 11
  //   Estrutura Código:
  //   2 BITS - 4 BITS - 4 BITS
  //   <opcode> - imediatoA - imediatoB
endmodule
