// Logisim project AP03.circ as structural Verilog: 1 circuit, main circuit main
// AP03
module main (
  input  [3:0] ENTRADA_1,
  input  [3:0] ENTRADA_B,
  input  S,
  input  S_OP,
  input  RESET_ALL,
  input  EN_AB,
  input  EN_C,
  output [3:0] OUTPUT
);

  wire CLOCK_out;
  wire [3:0] A_q, B_q, multiplexer_1_out, multiplexer_2_out, multiplexer_3_out, somador_1_output,
       subtrator_1_out;

  Clock CLOCK (.out(CLOCK_out));
  Multiplexer #(.width(4), .enable("false")) multiplexer_1 (
    .in0(OUTPUT), .in1(ENTRADA_1), .out(multiplexer_1_out), .sel(S));
  Multiplexer #(.width(4), .enable("false")) multiplexer_2 (
    .in0(A_q), .in1(ENTRADA_B), .out(multiplexer_2_out), .sel(S));
  Register #(.width(4)) A (.D(multiplexer_1_out), .en(EN_AB), .Q(A_q), .clk(CLOCK_out), .clr(RESET_ALL));
  Register #(.width(4)) B (.D(multiplexer_2_out), .en(EN_AB), .Q(B_q), .clk(CLOCK_out), .clr(RESET_ALL));
  SOMADOR somador_1 (.INPUT_1(A_q), .INPUT_2(B_q), .OUTPUT(somador_1_output));  // open: CARRY_OUT
  SUBTRATOR subtrator_1 (.A(A_q), .B(B_q), .OUT(subtrator_1_out));
  Multiplexer #(.width(4), .enable("false")) multiplexer_3 (
    .in0(somador_1_output), .in1(subtrator_1_out), .out(multiplexer_3_out), .sel(S_OP));
  Register #(.width(4)) C (.D(multiplexer_3_out), .en(EN_C), .Q(OUTPUT), .clk(CLOCK_out), .clr(RESET_ALL));
endmodule
