// Logisim project comparador.circ as structural Verilog: 1 circuit, main circuit COMPARADOR
module COMPARADOR (
  input  [3:0] INPUT_2,
  input  [3:0] INPUT_1,
  output OUTPUT
);

  wire and_1_out, and_3_out, xnor_1_out, xnor_2_out, xnor_3_out, xnor_4_out;

  xnor xnor_1 (xnor_1_out, INPUT_1[0], INPUT_2[0]);
  and and_1 (and_1_out, xnor_1_out, xnor_2_out);
  xnor xnor_2 (xnor_2_out, INPUT_2[1], INPUT_1[1]);
  xnor xnor_3 (xnor_3_out, INPUT_2[2], INPUT_1[2]);
  and and_2 (OUTPUT, and_1_out, and_3_out);
  xnor xnor_4 (xnor_4_out, INPUT_2[3], INPUT_1[3]);
  and and_3 (and_3_out, xnor_3_out, xnor_4_out);
endmodule
