// Logisim project full_adder.circ as structural Verilog: 1 circuit, main circuit FULL_ADDER
module FULL_ADDER (
  input  CARRY_IN,
  input  B1,
  input  B2,
  output SUM,
  output CARRY_OUT
);

  wire half_adder_1_carry_out, half_adder_1_sum, half_adder_2_carry_out;

  HALF_ADDER half_adder_1 (.B1(B1), .B2(B2), .SUM(half_adder_1_sum), .CARRY_OUT(half_adder_1_carry_out));
  HALF_ADDER half_adder_2 (.B1(CARRY_IN), .B2(half_adder_1_sum), .SUM(SUM), .CARRY_OUT(half_adder_2_carry_out));
  or or_1 (CARRY_OUT, half_adder_2_carry_out, half_adder_1_carry_out);
endmodule
