// Logisim project multiplicador.circ as structural Verilog: 1 circuit, main circuit MULTIPLICADOR
module MULTIPLICADOR (
  input  [3:0] A,
  input  [3:0] B,
  output [3:0] out,
  output CARRY_OUT
);

  wire a0_b1_out, a0_b2_out, a0_b3_out, A1_B0___A0__B1_carry_out, a1_b0_out, a1_b1_out, a1_b2_out, a2_b0_out,
       a2_b1_out, a3_b0_out, full_adder_1_carry_out, full_adder_1_sum, full_adder_2_carry_out,
       full_adder_3_carry_out, full_adder_3_sum, full_adder_4_carry_out, full_adder_4_sum;

  and a0_b0 (out[0], A[0], B[0]);
  and a1_b0 (a1_b0_out, A[1], B[0]);
  and a0_b1 (a0_b1_out, A[0], B[1]);
  and a2_b0 (a2_b0_out, A[2], B[0]);
  and a1_b1 (a1_b1_out, A[1], B[1]);
  and a0_b2 (a0_b2_out, A[0], B[2]);
  and a0_b3 (a0_b3_out, A[0], B[3]);
  and a3_b0 (a3_b0_out, A[3], B[0]);
  and a2_b1 (a2_b1_out, A[2], B[1]);
  and a1_b2 (a1_b2_out, A[1], B[2]);
  // AND_Gate a1_b3 has open pins: in0=A[1], in1=B[3], out=open
  // AND_Gate a3_b1 has open pins: in0=A[3], in1=B[1], out=open
  // AND_Gate a3_b2 has open pins: in0=A[3], in1=B[2], out=open
  // AND_Gate a2_b2 has open pins: in0=A[2], in1=B[2], out=open
  // AND_Gate a2_b3 has open pins: in0=A[2], in1=B[3], out=open
  // AND_Gate a3_b3 has open pins: in0=A[3], in1=B[3], out=open
  HALF_ADDER A1_B0___A0__B1 (.B1(a1_b0_out), .B2(a0_b1_out), .SUM(out[1]), .CARRY_OUT(A1_B0___A0__B1_carry_out));
  FULL_ADDER full_adder_1 (
    .B1(a2_b0_out), .B2(a1_b1_out), .CARRY_IN(A1_B0___A0__B1_carry_out), .SUM(full_adder_1_sum),
    .CARRY_OUT(full_adder_1_carry_out));
  FULL_ADDER full_adder_2 (
    .B1(full_adder_1_sum), .B2(a0_b2_out), .CARRY_IN(full_adder_1_carry_out), .SUM(out[2]),
    .CARRY_OUT(full_adder_2_carry_out));
  FULL_ADDER full_adder_3 (
    .B1(a3_b0_out), .B2(a2_b1_out), .CARRY_IN(full_adder_2_carry_out), .SUM(full_adder_3_sum),
    .CARRY_OUT(full_adder_3_carry_out));
  FULL_ADDER full_adder_4 (
    .B1(full_adder_3_sum), .B2(a1_b2_out), .CARRY_IN(full_adder_3_carry_out), .SUM(full_adder_4_sum),
    .CARRY_OUT(full_adder_4_carry_out));
  FULL_ADDER full_adder_5 (
    .B1(full_adder_4_sum), .B2(a0_b3_out), .CARRY_IN(full_adder_4_carry_out), .SUM(out[3]),
    .CARRY_OUT(CARRY_OUT));

  // Notes on the sheet:
  //   A
  //   A2*B0 + A1 *B1
  //   A2*B0 + A1 *B1 + A0*B2
  //   A3*B0 + A2 +B1
  //   A3*B0 + A2 +B1 + A1*B2
endmodule
