// Logisim project somador.circ as structural Verilog: 1 circuit, main circuit SOMADOR
module SOMADOR (
  input  [3:0] INPUT_1,
  input  [3:0] INPUT_2,
  output [3:0] OUTPUT,
  output CARRY_OUT
);

  wire full_adder_1_carry_out, full_adder_2_carry_out, full_adder_3_carry_out;

  FULL_ADDER full_adder_1 (
    .B1(INPUT_1[0]), .B2(INPUT_2[0]), .CARRY_IN(1'b0), .SUM(OUTPUT[0]), .CARRY_OUT(full_adder_1_carry_out));
  FULL_ADDER full_adder_2 (
    .B1(INPUT_1[1]), .B2(INPUT_2[1]), .CARRY_IN(full_adder_1_carry_out), .SUM(OUTPUT[1]),
    .CARRY_OUT(full_adder_2_carry_out));
  FULL_ADDER full_adder_3 (
    .B1(INPUT_1[2]), .B2(INPUT_2[2]), .CARRY_IN(full_adder_2_carry_out), .SUM(OUTPUT[2]),
    .CARRY_OUT(full_adder_3_carry_out));
  FULL_ADDER full_adder_4 (
    .B1(INPUT_2[3]), .B2(INPUT_1[3]), .CARRY_IN(full_adder_3_carry_out), .SUM(OUTPUT[3]),
    .CARRY_OUT(CARRY_OUT));
endmodule
