// Logisim project half_adder.circ as structural Verilog: 1 circuit, main circuit HALF_ADDER
module HALF_ADDER (
  input  B1,
  input  B2,
  output SUM,
  output CARRY_OUT
);

  xor xor_1 (SUM, B1, B2);
  and and_1 (CARRY_OUT, B1, B2);
endmodule
