// Logisim project subtrator.circ as structural Verilog: 1 circuit, main circuit Soma 4 Bits
module Soma_4_Bits (
  input  [3:0] X,
  input  [3:0] Y,
  input  Modo,
  output out_4,
  output [3:0] out_5
);

  wire fa_1_p5, fa_2_p5, fa_3_p5, xor_1_out, xor_2_out, xor_3_out, xor_4_out;

  xor xor_1 (xor_1_out, Modo, Y[0]);
  xor xor_2 (xor_2_out, Y[1], Modo);
  xor xor_3 (xor_3_out, Y[2], Modo);
  xor xor_4 (xor_4_out, Y[3], Modo);
  // FA fa_1: pin names not known; wires that end beside it: Modo, X[0], xor_1_out, out_5[0], fa_1_p5
  // FA fa_2: pin names not known; wires that end beside it: fa_1_p5, X[1], xor_2_out, out_5[1], fa_2_p5
  // FA fa_3: pin names not known; wires that end beside it: fa_2_p5, X[2], xor_3_out, out_5[2], fa_3_p5
  // FA fa_4: pin names not known; wires that end beside it: fa_3_p5, X[3], xor_4_out, out_5[3], out_4

  // Notes on the sheet:
  //   s0
endmodule
