// Logisim project AE_02_2025.circ as structural Verilog: 1 circuit, main circuit main
module main (
  output SEL_2,
  output [1:0] SEL_0,
  output [3:0] Output,
  output [1:0] SEL_1,
  output Op_FSM,
  output SEL_2_2
);

  wire clock_1_out, not_1_out, not_2_out, not_3_out, not_4_out, not_5_out, nST0_nOP_FSM_out,
       nST1_nST0_OP_FSM_out, nST2_nST1_ST0_out, ST0_q, ST1_2_q, ST1_nST0_out, ST1_out, ST1_ST0_out, ST2_2_q,
       ST2_nST0_out, ST2_out, ST2_ST0_out, ST3_out;
  wire [3:0] counter_1_q, multiplexer_1_out, multiplexer_2_out, multiplier_1_out, Reg_MULT_q, Reg_SUB_q,
       subtractor_1_out;
  wire [7:0] ram_1_data;

  Clock clock_1 (.out(clock_1_out));
  Counter #(.width(4), .max('hf)) counter_1 (
    .count(SEL_2), .Q(counter_1_q), .clk(clock_1_out));  // open: load, D, carry, clr
  or SEL_0_B1 (SEL_0[0], ST1_2_q, ST2_ST0_out);
  and ST2_nST0 (ST2_nST0_out, ST2_2_q, not_2_out);
  or ST2 (ST2_out, ST2_nST0_out, nST1_nST0_OP_FSM_out);
  or SEL_1_B0 (SEL_0[1], ST2_2_q, ST0_q);
  or nST1_nST0_OP_FSM (nST1_nST0_OP_FSM_out, not_1_out, not_2_out, Op_FSM);
  RAM #(.addrWidth(4), .dataWidth(9)) ram_1 (
    .addr(counter_1_q), .data({Op_FSM, ram_1_data}));  // open: sel, clk, ld, clr
  and ST2_ST0 (ST2_ST0_out, ST2_2_q, ST0_q);
  Register #(.width(1)) ST2_2 (.D(ST2_out), .Q(ST2_2_q), .clk(clock_1_out));  // open: en, clr
  not not_1 (not_1_out, ST1_2_q);
  not not_2 (not_2_out, ST0_q);
  or u_SEL_2 (SEL_2_2, ST2_2_q, ST1_2_q);
  not not_3 (not_3_out, ST2_2_q);
  and nST2_nST1_ST0 (nST2_nST1_ST0_out, not_1_out, not_3_out, ST0_q);
  or ST1 (ST1_out, nST2_nST1_ST0_out, ST1_nST0_out);
  Register #(.width(1)) ST1_2 (.D(ST1_out), .Q(ST1_2_q), .clk(clock_1_out));  // open: en, clr
  not not_4 (not_4_out, ST0_q);
  and ST1_nST0 (ST1_nST0_out, ST1_2_q, not_4_out);
  Multiplexer #(.select(2), .width(4), .enable("false")) multiplexer_1 (
    .in0(ram_1_data[3:0]), .in1(ram_1_data[7:4]), .in2(Reg_MULT_q), .in3(Reg_SUB_q), .out(multiplexer_1_out),
    .sel(SEL_0));
  Multiplexer #(.select(2), .width(4), .enable("false")) multiplexer_2 (
    .in0(ram_1_data[3:0]), .in1(ram_1_data[7:4]), .in2(Reg_MULT_q), .in3(Reg_SUB_q), .out(multiplexer_2_out),
    .sel({1'b0, SEL_1[0]}));
  Register #(.width(1)) ST0 (.D(ST3_out), .Q(ST0_q), .clk(clock_1_out));  // open: en, clr
  or ST3 (ST3_out, ST1_nST0_out, nST0_nOP_FSM_out);
  and nST0_nOP_FSM (nST0_nOP_FSM_out, not_2_out, not_5_out);
  Multiplier #(.width(4)) multiplier_1 (
    .a(multiplexer_1_out), .b(multiplexer_2_out), .out(multiplier_1_out));  // open: cin, cout
  Subtractor #(.width(4)) subtractor_1 (
    .a(multiplexer_1_out), .b(multiplexer_2_out), .out(subtractor_1_out));  // open: bin, bout
  not not_5 (not_5_out, Op_FSM);
  Register #(.width(4)) Reg_MULT (.D(multiplier_1_out), .Q(Reg_MULT_q), .clk(clock_1_out));  // open: en, clr
  Register #(.width(4)) Reg_SUB (.D(subtractor_1_out), .Q(Reg_SUB_q), .clk(clock_1_out));  // open: en, clr
  Multiplexer #(.width(4), .enable("false")) multiplexer_3 (
    .in0(Reg_MULT_q), .in1(Reg_SUB_q), .out(Output), .sel(SEL_2_2));
  and ST1_ST0 (ST1_ST0_out, ST1_2_q, ST0_q);
  or EN_PC (SEL_2, ST1_ST0_out, ST2_2_q);

  assign SEL_1[1] = 1'b0;

  // Notes on the sheet:
  //   OP_FSM,A,B
  //   b
endmodule
