// Logisim project PO_2.circ as structural Verilog: 1 circuit, main circuit main
module main (
  input  CLEAR,
  output [3:0] Output,
  output Op_FSM
);

  wire and_1_out, and_3_out, and_4_out, and_5_out, and_6_out, and_7_out, clock_1_out, not_1_out, or_2_out,
       or_3_out, or_4_out, ST0_qn, ST1_q, ST1_qn, ST2_qn;
  wire [1:0] or_1_out, ST2_q;
  wire [3:0] adder_1_out, counter_1_q, multiplexer_1_out, multiplexer_2_out, Reg_SOMA_q, Reg_SUB_q,
       subtractor_1_out;
  wire [7:0] ram_1_data;

  Clock clock_1 (.out(clock_1_out));
  Counter #(.width(4), .max('hf)) counter_1 (
    .count(or_4_out), .Q(counter_1_q), .clk(clock_1_out), .clr(CLEAR));  // open: load, D, carry
  and and_1 (and_1_out, ST2_q[1], ST1_q, ST2_qn);
  and and_2 (or_1_out[1], ST2_q[1], ST1_qn);
  D_Flip_Flop ST2 (.clk(clock_1_out), .D(and_1_out), .Q(ST2_q[0]), .Qn(ST2_qn));  // open: preset, en, reset
  RAM #(.addrWidth(4), .dataWidth(9)) ram_1 (
    .addr(counter_1_q), .data({Op_FSM, ram_1_data}));  // open: sel, clk, ld, clr
  or or_1 (or_1_out[0], ST2_q[1], ST1_qn);
  D_Flip_Flop ST1 (.clk(clock_1_out), .D(or_2_out), .Q(ST1_q), .Qn(ST1_qn));  // open: preset, en, reset
  D_Flip_Flop ST0 (.clk(clock_1_out), .D(or_3_out), .Q(ST2_q[1]), .Qn(ST0_qn));  // open: preset, en, reset
  Multiplexer #(.select(2), .width(4), .enable("false")) multiplexer_1 (
    .in0(ram_1_data[3:0]), .in1(ram_1_data[7:4]), .in2(Reg_SOMA_q), .in3(Reg_SUB_q), .out(multiplexer_1_out),
    .sel(ST2_q));
  Multiplexer #(.select(2), .width(4), .enable("false")) multiplexer_2 (
    .in0(ram_1_data[3:0]), .in1(ram_1_data[7:4]), .in2(Reg_SOMA_q), .in3(Reg_SUB_q), .out(multiplexer_2_out),
    .sel(or_1_out));
  and and_3 (and_3_out, Op_FSM, ST0_qn);
  and and_4 (and_4_out, ST2_qn, ST1_q);
  not not_1 (not_1_out, Op_FSM);
  and and_5 (and_5_out, not_1_out, ST0_qn);
  and and_6 (and_6_out, ST1_q, ST2_qn);
  Adder #(.width(4)) adder_1 (.a(multiplexer_1_out), .b(multiplexer_2_out), .out(adder_1_out));  // open: cin, cout
  Subtractor #(.width(4)) subtractor_1 (
    .a(multiplexer_1_out), .b(multiplexer_2_out), .out(subtractor_1_out));  // open: bin, bout
  or or_2 (or_2_out, and_3_out, and_4_out);
  or or_3 (or_3_out, and_5_out, and_6_out);
  Register #(.width(4)) Reg_SOMA (.D(adder_1_out), .Q(Reg_SOMA_q), .clk(clock_1_out));  // open: en, clr
  Register #(.width(4)) Reg_SUB (.D(subtractor_1_out), .Q(Reg_SUB_q), .clk(clock_1_out));  // open: en, clr
  Multiplexer #(.width(4), .enable("false")) multiplexer_3 (
    .in0(Reg_SOMA_q), .in1(Reg_SUB_q), .out(Output), .sel(1'b1));
  and and_7 (and_7_out, not_1_out, ST2_q[1], ST1_qn);
  or or_4 (or_4_out, and_7_out, ST2_q[0]);
endmodule
